# Fritzing sketch heartmonitor (saved by Fritzing 0.2.3)
breadboards: 1

parts:
  R1 = Basic Photo-Resistor (Photocell) [package=THT]  # not connected
  R3 = 10k Ω Resistor [package=THT]
  R7 = 10 Ω Resistor [package=THT]
  C3 = Electrolytic Capacitor [package=THT]
  R9 = 1.5k Ω Resistor [package=THT]
  C5 = Electrolytic Capacitor [package=THT]
  Arduino1 = Arduino Diecimila (deprecated) [package=THT]
  U1 = LM 358 Dual Op-Amp [package="DIP8 [THT]"]

nets:
  N1: R3.Pin_0, R9.Pin_1
  N2: R7.Pin_0, R7.Pin_1
  N3: C3.-, C3.+
  N4: C5.-, C5.+
  N5: Arduino1.A0, U1.connector6

notes:
  this is actually 1 ohm
  actually 1.8k ohm
